// Logisim project ALUKevin.circ as structural Verilog: 3 circuits, main circuit ALU
module ALU (
  input  [31:0] A,
  input  [31:0] B,
  input  [4:0] Shift,
  input  [3:0] in_4,
  input  CarryIn,
  output [31:0] S,
  output [3:0] Flags
);

  wire codop_1_adc, codop_1_asr, codop_1_bic, codop_1_cmn, codop_1_cmp, codop_1_lsl, codop_1_lsr,
       codop_1_mul, codop_1_mvn, codop_1_orr, codop_1_rorr, codop_1_rsb, codop_1_sbc, codop_1_tst;
  wire [1:0] codop_1_an;
  wire [31:0] controlled_inverter_1_out, undriven;

  Multiplexer #(.select(2), .width(32)) multiplexer_1 (.in1(undriven), .sel(codop_1_an));  // open: in0, in2, in3, out
  CODOP codop_1 (
    .a(in_4), .AN(codop_1_an[0]), .EOR(codop_1_an[1]), .LSL(codop_1_lsl), .LSR(codop_1_lsr),
    .ASR(codop_1_asr), .ADC(codop_1_adc), .SBC(codop_1_sbc), .RORr(codop_1_rorr), .TST(codop_1_tst),
    .RSB(codop_1_rsb), .CMP(codop_1_cmp), .CMN(codop_1_cmn), .ORR(codop_1_orr), .MUL(codop_1_mul),
    .BIC(codop_1_bic), .MVN(codop_1_mvn));
  // AND_Gate and_1 has open pins: in0=A, in1=B, out=open
  // XOR_Gate xor_1 has open pins: in0=A, in2=B, out=open
  Shifter #(.width(32)) shifter_1 (.in(B), .\dist (Shift));  // open: out
  Shifter #(.width(32)) shifter_2 (.in(B), .\dist (Shift));  // open: out
  Shifter #(.width(32)) shifter_3 (.in(B), .\dist (Shift));  // open: out
  Adder #(.width(32)) adder_1 (.a(A));  // open: b, out, cin, cout
  Subtractor #(.width(32)) subtractor_1 (.a(B), .b(A));  // open: out, bin, bout
  Subtractor subtractor_2 ();  // open: a, b, out, bin, bout
  Subtractor #(.width(32)) subtractor_3 (.b(A));  // open: a, out, bin, bout
  Subtractor #(.width(32)) subtractor_4 (.a(B), .b(A));  // open: out, bin, bout
  Adder #(.width(32)) adder_2 (.a(A), .b(B));  // open: out, cin, cout
  // OR_Gate or_1 has open pins: in0=A, in1=B, out=open
  Multiplier #(.width(32)) multiplier_1 (.a(A), .b(B));  // open: out, cin, cout
  Controlled_Inverter #(.width(32)) controlled_inverter_1 (.in(A), .out(controlled_inverter_1_out));  // open: en
  Controlled_Inverter #(.width(32)) controlled_inverter_2 (.in(A));  // open: out, en
  Adder adder_3 ();  // open: a, b, out, cin, cout
  // AND_Gate and_2 has open pins: in0=controlled_inverter_1_out, in1=B, out=open

  // Notes on the sheet:
  //   Note: for ROR, C = N
  //   Note 2: assume that shift > 0 for LSL and LSR
endmodule

module BancRegistre (
  input  [31:0] DataIn,
  input  [2:0] RegA,
  input  [2:0] RegB,
  input  [2:0] RegDest,
  input  Clk,
  input  Reset,
  output [31:0] AOut,
  output [31:0] BOut,
  output [31:0] R0,
  output [31:0] R1,
  output [31:0] R2,
  output [31:0] R3,
  output [31:0] R4,
  output [31:0] R5,
  output [31:0] R6,
  output [31:0] R7
);

  ALU alu_1 ();  // open: A, B, Shift, in_4, CarryIn, S, Flags
endmodule

module CODOP (
  input  [3:0] a,
  output AN,
  output EOR,
  output LSL,
  output LSR,
  output ASR,
  output ADC,
  output SBC,
  output RORr,
  output TST,
  output RSB,
  output CMP,
  output CMN,
  output ORR,
  output MUL,
  output BIC,
  output MVN
);

  wire not_1_out, not_2_out, not_3_out, not_4_out;

  not not_1 (not_1_out, a[3]);
  not not_2 (not_2_out, a[2]);
  not not_3 (not_3_out, a[1]);
  not not_4 (not_4_out, a[0]);
  and and_1 (AN, not_1_out, not_2_out, not_3_out, not_4_out);
  and and_2 (EOR, not_1_out, not_2_out, not_3_out, a[0]);
  and and_3 (LSL, not_1_out, not_2_out, a[1], not_4_out);
  and and_4 (LSR, not_1_out, not_2_out, a[1], a[0]);
  and and_5 (ASR, not_1_out, a[2], not_3_out, not_4_out);
  and and_6 (ADC, not_1_out, a[2], not_3_out, a[0]);
  and and_7 (SBC, not_1_out, a[2], a[1], not_4_out);
  and and_8 (RORr, not_1_out, a[2], a[1], a[0]);
  and and_9 (TST, a[3], not_2_out, not_3_out, not_4_out);
  and and_10 (RSB, a[3], not_2_out, not_3_out, a[0]);
  and and_11 (CMP, a[3], not_2_out, a[1], not_4_out);
  and and_12 (CMN, a[3], not_2_out, a[1], a[0]);
  and and_13 (ORR, a[3], a[2], not_3_out, not_4_out);
  and and_14 (MUL, a[3], a[2], not_3_out, a[0]);
  and and_15 (BIC, a[3], a[2], a[1], not_4_out);
  and and_16 (MVN, a[3], a[2], a[1], a[0]);
endmodule
